# Fritzing sketch circuit-sketch (saved by Fritzing 0.9.2b)
breadboards: 1

parts:
  Part1 = SparkFun ESP8266 Thing
  R1 = TRIMPOT [package=3386u]
  R2 = Resistor [tolerance=±5% resistance=10k package="2010 [SMD]"]
  R3 = Resistor [tolerance=±5% resistance=10k package="2010 [SMD]"]
  R4 = Resistor [tolerance=±5% resistance=10k package="2010 [SMD]"]
  LED1 = LEDs [package=led10mm]
  R5 = Resistor [tolerance=±5% resistance=330 package="2010 [SMD]"]
  LED2 = LEDs [package=led10mm]
  R6 = Resistor [tolerance=±5% resistance=330 package="2010 [SMD]"]

nets:
  N1: Part1.USBVCC, R2.Pin_0
  N2: Part1.GND, R1.CW, R4.Pin_1, R5.Pin_1, R6.Pin_1
  N3: Part1.GPIO4, LED2.A
  N4: Part1.GPIO13, LED1.A
  N5: Part1.ADC, R1.WIPER
  N6: R1.CCW, R3.Pin_1, R4.Pin_0
  N7: R2.Pin_1, R3.Pin_0
  N8: LED1.C, R5.Pin_0
  N9: LED2.C, R6.Pin_0
